// Logisim project game_of_life.circ as structural Verilog: 2 circuits, main circuit main
module game_of_life_cell (
  input  D,
  input  CLK,
  input  RST,
  input  NW,
  input  N,
  input  NE,
  input  W,
  input  E,
  input  SW,
  input  S,
  input  SE,
  output out_12
);

  wire and_1_out, comparator_1_eq, comparator_2_eq, register_1_q;
  wire [3:0] bitadder_1_out;

  Register #(.width(1)) register_1 (.D(D), .clk(CLK), .Q(register_1_q), .clr(RST));  // open: en
  BitAdder bitadder_1 (.in0({SE, S, SW, E, W, NE, N, NW}), .out(bitadder_1_out));
  Comparator #(.width(4)) comparator_1 (.a(bitadder_1_out), .b(4'b0010), .eq(comparator_1_eq));  // open: gt, lt
  Comparator #(.width(4)) comparator_2 (.a(bitadder_1_out), .b(4'b0011), .eq(comparator_2_eq));  // open: gt, lt
  and and_1 (and_1_out, register_1_q, comparator_1_eq);
  or or_1 (out_12, and_1_out, comparator_2_eq);

  // Other names for the same wires on the sheet: next_state = out_12
endmodule

module main (
  input  RESET
);

  wire C11, C12, C13, C14, C21, C22, C23, C24, C31, C32, C33, C34, C41, C42, C43, C44, CLK;

  Clock clock_1 (.out(CLK));
  game_of_life_cell game_of_life_cell_1 (
    .CLK(CLK), .RST(RESET), .NW(C44), .N(C41), .NE(C42), .W(C14), .E(C12), .SW(C24), .S(C21), .SE(C22),
    .out_12(C11));  // open: D
  game_of_life_cell game_of_life_cell_2 (
    .CLK(CLK), .RST(RESET), .NW(C44), .N(C11), .NE(C12), .W(C24), .E(C22), .SW(C34), .S(C31), .SE(C32),
    .out_12(C21));  // open: D
  game_of_life_cell game_of_life_cell_3 (
    .CLK(CLK), .RST(RESET), .NW(C24), .N(C21), .NE(C22), .W(C34), .E(C32), .SW(C44), .S(C41), .SE(C42),
    .out_12(C31));  // open: D
  game_of_life_cell game_of_life_cell_4 (
    .CLK(CLK), .RST(RESET), .NW(C34), .N(C31), .NE(C32), .W(C44), .E(C42), .SW(C14), .S(C11), .SE(C12),
    .out_12(C41));  // open: D
  game_of_life_cell game_of_life_cell_5 (
    .CLK(CLK), .RST(RESET), .NW(C41), .N(C42), .NE(C43), .W(C11), .E(C13), .SW(C21), .S(C22), .SE(C23),
    .out_12(C12));  // open: D
  game_of_life_cell game_of_life_cell_6 (
    .CLK(CLK), .RST(RESET), .NW(C11), .N(C12), .NE(C13), .W(C21), .E(C23), .SW(C31), .S(C32), .SE(C33),
    .out_12(C22));  // open: D
  game_of_life_cell game_of_life_cell_7 (
    .CLK(CLK), .RST(RESET), .NW(C21), .N(C22), .NE(C23), .W(C21), .E(C23), .SW(C41), .S(C42), .SE(C43),
    .out_12(C32));  // open: D
  game_of_life_cell game_of_life_cell_8 (
    .CLK(CLK), .RST(RESET), .NW(C31), .N(C32), .NE(C33), .W(C41), .E(C43), .SW(C11), .S(C12), .SE(C13),
    .out_12(C42));  // open: D
  game_of_life_cell game_of_life_cell_9 (
    .CLK(CLK), .RST(RESET), .NW(C42), .N(C43), .NE(C44), .W(C12), .E(C14), .SW(C22), .S(C23), .SE(C24),
    .out_12(C13));  // open: D
  game_of_life_cell game_of_life_cell_10 (
    .CLK(CLK), .RST(RESET), .NW(C12), .N(C13), .NE(C14), .W(C22), .E(C24), .SW(C32), .S(C33), .SE(C34),
    .out_12(C23));  // open: D
  game_of_life_cell game_of_life_cell_11 (
    .CLK(CLK), .RST(RESET), .NW(C22), .N(C23), .NE(C24), .W(C32), .E(C34), .SW(C42), .S(C43), .SE(C44),
    .out_12(C33));  // open: D
  game_of_life_cell game_of_life_cell_12 (
    .CLK(CLK), .RST(RESET), .NW(C32), .N(C33), .NE(C34), .W(C42), .E(C43), .SW(C12), .S(C13), .SE(C14),
    .out_12(C43));  // open: D
  game_of_life_cell game_of_life_cell_13 (
    .CLK(CLK), .RST(RESET), .NW(C43), .N(C44), .NE(C41), .W(C13), .E(C11), .SW(C23), .S(C24), .SE(C21),
    .out_12(C14));  // open: D
  game_of_life_cell game_of_life_cell_14 (
    .CLK(CLK), .RST(RESET), .NW(C13), .N(C14), .NE(C11), .W(C23), .E(C21), .SW(C33), .S(C34), .SE(C31),
    .out_12(C24));  // open: D
  game_of_life_cell game_of_life_cell_15 (
    .CLK(CLK), .RST(RESET), .NW(C23), .N(C24), .NE(C21), .W(C33), .E(C31), .SW(C43), .S(C44), .SE(C11),
    .out_12(C34));  // open: D
  game_of_life_cell game_of_life_cell_16 (
    .CLK(CLK), .RST(RESET), .NW(C33), .N(C34), .NE(C31), .W(C43), .E(C41), .SW(C13), .S(C14), .SE(C11),
    .out_12(C44));  // open: D

  // Other names for the same wires on the sheet: RST = RESET
endmodule
